# Fritzing sketch ArduFarmBot Light (saved by Fritzing 0.9.3b)
breadboards: 1

parts:
  Part1 = Arduino Uno (Rev3)
  ESP-01 = ESP8266 WiFi Module [part_number=ESP8266]
  Actuator_1 = LED - 5mm [color="Red (633nm)" package="5 mm [THT]"]
  Actuator_2 = LED - 5mm [color="Green (565nm)" package="5 mm [THT]"]
  R1 = Resistor [tolerance=±5% resistance=330 package=THT]
  R2 = Resistor [tolerance=±5% resistance=330 package=THT]
  LM394 = LM393 [part_number=COMPARATOR package=so08]
  YL-70 = Soil Moisture Sensor [part_number="SOIL MOISTURE SENSOR"]
  Temperature_Sensor = DS18B20 1-Wire Temperature Sensor [part_number=DS18B20]
  DHT22 = Humidity and Temperature Sensor RHT03 [part_number="TEMP/HUM SENSOR"]
  R5 = Resistor [tolerance=±5% resistance=10k package=THT]
  R6 = Resistor [tolerance=±5% resistance=4.7k package=THT]
  R7 = Resistor [tolerance=±5% resistance=10k package=THT]
  LDR = Photocell (LDR) [package=THT]
  EXTERNAL = Power Jack [part_number="POWER 5V" package=power_jack_smd]
  EXTERNAL1 = Power Jack [part_number="POWER 5V" package=power_jack_smd]  # not connected
  5V_Pump1 = Solenoid
  220V_Lamp1 = LEDs [package=led10mm]
  U5 = 2-Channel 5v Relay Shield [package=relay-2ch5v10a]
  EXTERNAL4 = Power Jack [part_number="POWER 220V" package=power_jack_smd]
  EXTERNAL5 = Power Jack [part_number="POWER 5V" package=power_jack_smd]

nets:
  N1: Part1.A0, LM394.G2_OUT
  N2: Part1.A1, R7.Pin_1, LDR.pin_0
  N3: Part1.D8, ESP-01.GPIO_16
  N4: Part1.D10_PWM/SS, Actuator_1.anode, R1.Pin_0, U5.IN1
  N5: Part1.D11_PWM/MOSI, DHT22.Data-signal, R5.Pin_1
  N6: Part1.D12/MISO, Actuator_2.cathode, U5.IN2
  GND: Part1.GND, ESP-01.GND, LM394.G1_V-, Temperature_Sensor.GND, DHT22.GND_2, LDR.pin_1
  N7: Part1.D5_PWM, Temperature_Sensor.DQ, R6.Pin_1
  N8: Part1.D6_PWM, ESP-01.TXD
  N9: Part1.D7, ESP-01.RXD
  3V3: Part1.3V3, ESP-01.VCC, ESP-01.CH_PD
  VCC: Part1.5V, R1.Pin_1, R2.Pin_1, LM394.G1_V+, Temperature_Sensor.VDD, DHT22.Vcc, R5.Pin_0, R6.Pin_0, R7.Pin_0, U5.VCC
  N10: Actuator_2.anode, R2.Pin_0
  N11: LM394.G1_-IN, YL-70.VCC
  N12: LM394.G1_+IN, YL-70.SIG
  N13: EXTERNAL.GND, U5.JD-GND
  N14: 5V_Pump1.pin2, U5.K1-On
  N15: 220V_Lamp1.C, U5.K2-In
  N16: 220V_Lamp1.A, EXTERNAL4.GND
  N17: U5.K1-In, EXTERNAL5.GND
  N18: U5.K2-On, EXTERNAL4.GNDBREAK

notes:
  NO1
  NO2

custom parts:
  ESP8266 WiFi Module: Generic WiFi Module based on the ESP8266 with onboard PCB antenna and UART communications
  2-Channel 5v Relay Shield: 2 Channel 5v Relay Shield w. 2x SPD-06VDC-SD-C
