# Fritzing sketch ESP-01 UNO (saved by Fritzing 0.9.3b)
breadboards: 1

parts:
  Part1 = Arduino Uno (Rev3)
  ESP-01 = ESP8266 WiFi Module [part_number=ESP8266]

nets:
  N1: Part1.D8, ESP-01.GPIO_16
  N2: Part1.D6_PWM, ESP-01.TXD
  N3: Part1.D7, ESP-01.RXD
  3V3: Part1.3V3, ESP-01.VCC, ESP-01.CH_PD
  GND: Part1.GND, ESP-01.GND

custom parts:
  ESP8266 WiFi Module: Generic WiFi Module based on the ESP8266 with onboard PCB antenna and UART communications
