# Fritzing sketch ArduFarmBot Light Actuators (saved by Fritzing 0.9.3b)
breadboards: 1

parts:
  Part1 = Arduino Uno (Rev3)
  ESP-01 = ESP8266 WiFi Module [part_number=ESP8266]
  Actuator_1 = LED - 5mm [color="Red (633nm)" package="5 mm [THT]"]
  Actuator_2 = LED - 5mm [color="Green (565nm)" package="5 mm [THT]"]
  R1 = Resistor [tolerance=±5% resistance=330 package=THT]
  R2 = Resistor [tolerance=±5% resistance=330 package=THT]
  U4 = 2-Channel 5v Relay Shield [package=relay-2ch5v10a]
  EXTERNAL = Power Jack [part_number="POWER 5V" package=power_jack_smd]
  EXTERNAL1 = Power Jack [part_number="POWER 5V" package=power_jack_smd]  # not connected
  5V_Pump = Solenoid
  EXTERNAL2 = Power Jack [part_number="POWER 5V" package=power_jack_smd]
  220V_Lamp = LEDs [package=led10mm]
  EXTERNAL3 = Power Jack [part_number="POWER 220V" package=power_jack_smd]

nets:
  N1: Part1.D8, ESP-01.GPIO_16
  N2: Part1.D10_PWM/SS, Actuator_1.anode, R1.Pin_0, U4.IN1
  N3: Part1.D12/MISO, Actuator_2.cathode, U4.IN2
  GND: Part1.GND, ESP-01.GND
  N4: Part1.D6_PWM, ESP-01.TXD
  N5: Part1.D7, ESP-01.RXD
  3V3: Part1.3V3, ESP-01.VCC, ESP-01.CH_PD
  5V: Part1.5V, U4.VCC
  N6: Actuator_2.anode, R2.Pin_0
  N7: R1.Pin_1, R2.Pin_1
  N8: U4.K1-In, EXTERNAL2.GND
  N9: U4.K1-On, 5V_Pump.pin2
  N10: U4.K2-In, 220V_Lamp.C
  N11: U4.K2-On, EXTERNAL3.GNDBREAK
  N12: U4.JD-GND, EXTERNAL.GND
  N13: 220V_Lamp.A, EXTERNAL3.GND

notes:
  NO2
  NO1

custom parts:
  ESP8266 WiFi Module: Generic WiFi Module based on the ESP8266 with onboard PCB antenna and UART communications
  2-Channel 5v Relay Shield: 2 Channel 5v Relay Shield w. 2x SPD-06VDC-SD-C
