# Fritzing sketch ArduFarmBot Light Sensors ESP (saved by Fritzing 0.9.3b)
breadboards: 1

parts:
  Part1 = Arduino Uno (Rev3)
  ESP-01 = ESP8266 WiFi Module [part_number=ESP8266]
  LM394 = LM393 [part_number=COMPARATOR package=so08]
  YL-70 = Soil Moisture Sensor [part_number="SOIL MOISTURE SENSOR"]
  Temperature_Sensor = DS18B20 1-Wire Temperature Sensor [part_number=DS18B20]
  DHT22 = Humidity and Temperature Sensor RHT03 [part_number="TEMP/HUM SENSOR"]
  R5 = Resistor [tolerance=±5% resistance=10k package=THT]
  R6 = Resistor [tolerance=±5% resistance=4.7k package=THT]
  R7 = Resistor [tolerance=±5% resistance=10k package=THT]
  LDR = Photocell (LDR) [package=THT]

nets:
  N1: Part1.A0, LM394.G2_OUT
  N2: Part1.A1, R7.Pin_1, LDR.pin_0
  N3: Part1.D8, ESP-01.GPIO_16
  N4: Part1.D11_PWM/MOSI, DHT22.Data-signal, R5.Pin_1
  GND: Part1.GND, ESP-01.GND, LM394.G1_V-, Temperature_Sensor.GND, DHT22.GND_2, LDR.pin_1
  N5: Part1.D5_PWM, Temperature_Sensor.DQ, R6.Pin_1
  N6: Part1.D6_PWM, ESP-01.TXD
  N7: Part1.D7, ESP-01.RXD
  3V3: Part1.3V3, ESP-01.VCC, ESP-01.CH_PD
  5V: Part1.5V, LM394.G1_V+, Temperature_Sensor.VDD, DHT22.Vcc, R5.Pin_0, R6.Pin_0, R7.Pin_0
  N8: LM394.G1_-IN, YL-70.VCC
  N9: LM394.G1_+IN, YL-70.SIG

custom parts:
  ESP8266 WiFi Module: Generic WiFi Module based on the ESP8266 with onboard PCB antenna and UART communications
