# Fritzing sketch ArduFarmBot Light - Sensors (saved by Fritzing 0.9.3b)
breadboards: 1

parts:
  Part1 = Arduino Uno (Rev3)
  LM394 = LM393 [part_number=COMPARATOR package=so08]
  YL-70 = Soil Moisture Sensor [part_number="SOIL MOISTURE SENSOR"]
  Temperature_Sensor = DS18B20 1-Wire Temperature Sensor [part_number=DS18B20]
  DHT22 = Humidity and Temperature Sensor RHT03 [part_number="TEMP/HUM SENSOR"]
  R5 = Resistor [tolerance=±5% resistance=10k package=THT]
  R6 = Resistor [tolerance=±5% resistance=4.7k package=THT]
  R7 = Resistor [tolerance=±5% resistance=10k package=THT]
  LDR = Photocell (LDR) [package=THT]

nets:
  N1: Part1.A0, LM394.G2_OUT
  N2: Part1.A1, R7.Pin_1, LDR.pin_0
  N3: Part1.D11_PWM/MOSI, DHT22.Data-signal, R5.Pin_1
  GND: Part1.GND, LM394.G1_V-, Temperature_Sensor.GND, DHT22.GND_2, LDR.pin_1
  N4: Part1.D5_PWM, Temperature_Sensor.DQ, R6.Pin_1
  5V: Part1.5V, LM394.G1_V+, Temperature_Sensor.VDD, DHT22.Vcc, R5.Pin_0, R6.Pin_0, R7.Pin_0
  N5: LM394.G1_-IN, YL-70.VCC
  N6: LM394.G1_+IN, YL-70.SIG
